// Logisim project RiscVComputer.circ as structural Verilog: 14 circuits, main circuit main
module main (
  input  RESET
);

  wire ALUSrc, branch_taken, CLK, IsBranch, IsJAL, IsJALR, MemRead, MemWrite, RegWrite, take_target;
  wire [1:0] ALUOp, ASel, WBSel;
  wire [2:0] funct3, ImmSel;
  wire [3:0] ALUCtrl;
  wire [4:0] rd, rs1, rs2;
  wire [6:0] funct7, opcode;
  wire [31:0] alu_a, alu_b, alu_result, imm, instr, jalr_target, mem_rdata, next_pc, pc, pc_a, pc_plus4,
       pc_target, rs1_data, rs2_data, wb_data;

  Clock clock_1 (.out(CLK));
  Register #(.width(32)) u_PC (.D(next_pc), .en(1'b1), .clk(CLK), .Q(pc), .clr(RESET));
  // Probe on pc
  Adder #(.width(32)) adder_1 (.a(pc), .b(32'h4), .out(pc_plus4));  // open: cin, cout
  ROM #(.addrWidth(8), .dataWidth(32)) rom_1 (.addr(pc[9:2]), .data(instr));
  // Probe on instr
  InstructionDecode instructiondecode_1 (
    .Instruction(instr), .funct7(funct7), .rs2(rs2), .rs1(rs1), .funct3(funct3), .rd(rd), .opcode(opcode));
  MainControl maincontrol_1 (
    .opcode(opcode), .RegWrite(RegWrite), .ALUSrc(ALUSrc), .MemWrite(MemWrite), .MemRead(MemRead),
    .IsBranch(IsBranch), .ALUOp(ALUOp), .ImmSel(ImmSel), .ASel(ASel), .WBSel(WBSel), .IsJAL(IsJAL),
    .IsJALR(IsJALR));
  ImmGen immgen_1 (.Instruction(instr), .ImmSel(ImmSel), .Imm(imm));
  RegisterFile registerfile_1 (
    .write_data(wb_data), .CLK(CLK), .write(RegWrite), .rd(rd), .rs1(rs1), .rs2(rs2), .rs1_data(rs1_data),
    .rs2_data(rs2_data));
  // Probe on alu_result
  Multiplexer #(.select(2), .width(32)) multiplexer_1 (
    .in0(rs1_data), .in1(pc), .in2({32{1'b0}}), .in3({32{1'b0}}), .out(alu_a), .sel(ASel));
  Multiplexer #(.select(1), .width(32)) multiplexer_2 (.in0(rs2_data), .in1(imm), .out(alu_b), .sel(ALUSrc));
  Adder #(.width(32)) adder_2 (.a(pc), .b(imm), .out(pc_target));  // open: cin, cout
  assign jalr_target = alu_result & 32'hfffffffe;  // AND_Gate and_1, 32 bits wide
  or or_1 (take_target, branch_taken, IsJAL);
  // Probe on branch_taken
  ALUControl alucontrol_1 (.funct7(funct7), .ALUOp(ALUOp), .funct3(funct3), .ALUCtrl(ALUCtrl));
  ALU alu_1 (.rs1_data(alu_a), .rs2_data(alu_b), .ALU_Ctrl(ALUCtrl), .result(alu_result));
  BranchUnit branchunit_1 (
    .rs1_data(rs1_data), .rs2_data(rs2_data), .IsBranch(IsBranch), .funct3(funct3),
    .branch_taken(branch_taken));
  Multiplexer #(.select(1), .width(32)) multiplexer_3 (.in0(pc_plus4), .in1(pc_target), .out(pc_a), .sel(take_target));
  Multiplexer #(.select(1), .width(32)) multiplexer_4 (.in0(pc_a), .in1(jalr_target), .out(next_pc), .sel(IsJALR));
  // Probe on wb_data
  Memory memory_1 (
    .Address(alu_result), .write_data(rs2_data), .MemWrite(MemWrite), .CLK(CLK), .funct3(funct3),
    .read_data(mem_rdata));
  Multiplexer #(.select(2), .width(32)) multiplexer_5 (
    .in0(alu_result), .in1(mem_rdata), .in2(pc_plus4), .in3({32{1'b0}}), .out(wb_data), .sel(WBSel));

  // Other names for the same wires on the sheet: pc_word[7:0] = pc[9:2]

  // Notes on the sheet:
  //   Clock: Ctrl+F9 = 1 full cycle
  //   RESET = 1 holds PC at 0
  //   PC register
  //   BẢNG THEO DÕI (probe): xem các giá trị này sau mỗi lần bấm Ctrl+F9
  //   IF - Instruction Fetch
  //   PC: địa chỉ lệnh đang được nạp
  //   (tăng 4 mỗi chu kỳ, nhảy khi rẽ nhánh)
  //   PC[9:2] = word address
  //   PC + 4
  //   contents of rom_1 (hex, n*v repeats v):
  //   00000513 00a00593 00b50533 fff58593 fe059ce3 00a02023 00002603 010000ef 40a606b3 0646a713 0000006f
  //   00c60633 00008067 00000000 00000000 00000000
  //   Instruction ROM 256 x 32
  //   instr: mã máy 32-bit của lệnh
  //   đang thực thi (đọc từ ROM)
  //   RV32I single-cycle CPU - top level
  //   One instruction per clock cycle.  Data flows left to right: IF > ID > EX > MEM > WB.  Tunnels with the same name are the same wire.
  //   ID - Decode / Register Read
  //   InstructionDecode
  //   MainControl
  //   ImmGen
  //   RegisterFile
  //   alu_result: kết quả ALU
  //   (số học, địa chỉ load/store)
  //   Next PC
  //   ALU operand A: 00 rs1   01 PC (auipc)   10 zero (lui)
  //   ALU operand B: 0 rs2   1 imm
  //   PC + imm (branch / JAL target)
  //   JALR target = (rs1 + imm) with bit 0 cleared
  //   EX - Execute and next PC
  //   branch_taken: 1 = lệnh rẽ nhánh
  //   được rẽ, PC nhảy tới đích
  //   ALUControl
  //   ALU
  //   BranchUnit (beq bne blt bge bltu bgeu)
  //   take_target = branch taken OR JAL
  //   IsJALR selects the register jump
  //   wb_data: giá trị ghi vào thanh ghi rd
  //   ở cuối chu kỳ (write-back)
  //   MEM - Data Memory
  //   Memory (lb lh lw lbu lhu sb sh sw)
  //   WBSel: 00 ALU   01 memory   10 PC+4 (JAL/JALR)
  //   WB - Write Back
endmodule

module ALU (
  input  [31:0] rs1_data,
  input  [31:0] rs2_data,
  input  [3:0] ALU_Ctrl,
  output [31:0] result
);

  wire comparator_1_lt, comparator_2_lt;
  wire [31:0] adder_1_out, and_1_out, bit_extender_1_out, bit_extender_2_out, or_1_out, shifter_1_out,
       shifter_2_out, shifter_3_out, subtractor_1_out, xor_1_out;

  Adder #(.width(32)) adder_1 (.a(rs1_data), .b(rs2_data), .out(adder_1_out));  // open: cin, cout
  Subtractor #(.width(32)) subtractor_1 (.a(rs1_data), .b(rs2_data), .out(subtractor_1_out));  // open: bin, bout
  Shifter #(.width(32)) shifter_1 (.in(rs1_data), .\dist (rs2_data[4:0]), .out(shifter_1_out));
  Shifter #(.shift("lr"), .width(32)) shifter_2 (.in(rs1_data), .\dist (rs2_data[4:0]), .out(shifter_2_out));
  Shifter #(.shift("ar"), .width(32)) shifter_3 (.in(rs1_data), .\dist (rs2_data[4:0]), .out(shifter_3_out));
  Comparator #(.width(32)) comparator_1 (.a(rs1_data), .b(rs2_data), .lt(comparator_1_lt));  // open: gt, eq
  Comparator #(.mode("unsigned"), .width(32)) comparator_2 (
    .a(rs1_data), .b(rs2_data), .lt(comparator_2_lt));  // open: gt, eq
  assign and_1_out = rs1_data & rs2_data;  // AND_Gate and_1, 32 bits wide
  assign or_1_out = rs1_data | rs2_data;  // OR_Gate or_1, 32 bits wide
  assign xor_1_out = rs1_data ^ rs2_data;  // XOR_Gate xor_1, 32 bits wide
  assign bit_extender_1_out = {{31{1'b0}}, comparator_1_lt};  // Bit_Extender bit_extender_1
  assign bit_extender_2_out = {{31{1'b0}}, comparator_2_lt};  // Bit_Extender bit_extender_2
  Multiplexer #(.select(4), .width(32)) multiplexer_1 (
    .in0(adder_1_out), .in1(subtractor_1_out), .in2(and_1_out), .in3(or_1_out), .in4(xor_1_out),
    .in5(shifter_1_out), .in6(shifter_2_out), .in7(shifter_3_out), .in8(bit_extender_1_out),
    .in9(bit_extender_2_out), .out(result), .sel(ALU_Ctrl));  // open: in10, in11, in12, in13, in14, in15
  // Probe on result

  // Notes on the sheet:
  //   ALU
  //   Every operation is computed in parallel; ALU_Ctrl selects which result leaves the ALU.
  //   ADD   (ctrl 0)
  //   SUB   (ctrl 1)
  //   AND   (ctrl 2)
  //   OR   (ctrl 3)
  //   XOR   (ctrl 4)
  //   SLL (ctrl 5)
  //   SRL (ctrl 6)
  //   SRA (ctrl 7)
  //   SRA: arithmetic shift right
  //   SLT
  //   SLTU
  //   ALU_Ctrl  operation
  //   0 ADD   1 SUB   2 AND   3 OR   4 XOR
  //   5 SLL   6 SRL   7 SRA
  //   8 SLT (signed)   9 SLTU (unsigned)
  //   SLT and SLTU: the 1-bit compare result is zero-extended,
  //   so the ALU output is 0x00000000 or 0x00000001.
endmodule

module InstructionDecode (
  input  [31:0] Instruction,
  output [6:0] funct7,
  output [4:0] rs2,
  output [4:0] rs1,
  output [2:0] funct3,
  output [4:0] rd,
  output [6:0] opcode
);


  assign funct3 = Instruction[14:12];
  assign funct7 = Instruction[31:25];
  assign opcode = Instruction[6:0];
  assign rd = Instruction[11:7];
  assign rs1 = Instruction[19:15];
  assign rs2 = Instruction[24:20];

  // Notes on the sheet:
  //   InstructionDecode
  //   Pure wiring (one splitter): cuts the 32-bit instruction into its RISC-V fields.
  //   Field = instruction bits  ->  used by
  //   opcode = instr[6:0]  ->  MainControl (what kind of instruction)
  //   rd = instr[11:7]  ->  RegisterFile write address
  //   funct3 = instr[14:12]  ->  ALUControl, BranchUnit, Memory
  //   rs1 = instr[19:15]  ->  RegisterFile read address 1
  //   rs2 = instr[24:20]  ->  RegisterFile read address 2
  //   funct7 = instr[31:25]  ->  ALUControl (ADD vs SUB, SRL vs SRA)
endmodule

module RegisterFile (
  input  [31:0] write_data,
  input  CLK,
  input  write,
  input  [4:0] rd,
  input  [4:0] rs1,
  input  [4:0] rs2,
  output [31:0] rs1_data,
  output [31:0] rs2_data
);

  wire demultiplexer_1_out0, WE0, WE1, WE2, WE3, WE4, WE5, WE6, WE7, WE8, WE9, WE10, WE11, WE12, WE13, WE14,
       WE15, WE16, WE17, WE18, WE19, WE20, WE21, WE22, WE23, WE24, WE25, WE26, WE27, WE28, WE29, WE30, WE31;
  wire [31:0] X0, X1, X2, X3, X4, X5, X6, X7, X8, X9, X10, X11, X12, X13, X14, X15, X16, X17, X18, X19, X20,
       X21, X22, X23, X24, X25, X26, X27, X28, X29, X30, X31;

  Register #(.width(32)) u_x0 (.D({32{1'b0}}), .en(WE0), .clk(CLK), .Q(X0));  // open: clr
  Register #(.width(32)) u_x1 (.D(write_data), .en(WE1), .clk(CLK), .Q(X1));  // open: clr
  Register #(.width(32)) u_x2 (.D(write_data), .en(WE2), .clk(CLK), .Q(X2));  // open: clr
  Register #(.width(32)) u_x3 (.D(write_data), .en(WE3), .clk(CLK), .Q(X3));  // open: clr
  Register #(.width(32)) u_x4 (.D(write_data), .en(WE4), .clk(CLK), .Q(X4));  // open: clr
  Register #(.width(32)) u_x5 (.D(write_data), .en(WE5), .clk(CLK), .Q(X5));  // open: clr
  Register #(.width(32)) u_x6 (.D(write_data), .en(WE6), .clk(CLK), .Q(X6));  // open: clr
  Register #(.width(32)) u_x7 (.D(write_data), .en(WE7), .clk(CLK), .Q(X7));  // open: clr
  Multiplexer #(.select(5), .width(32)) multiplexer_1 (
    .in0(X0), .in1(X1), .in2(X2), .in3(X3), .in4(X4), .in5(X5), .in6(X6), .in7(X7), .in8(X8), .in9(X9),
    .in10(X10), .in11(X11), .in12(X12), .in13(X13), .in14(X14), .in15(X15), .in16(X16), .in17(X17),
    .in18(X18), .in19(X19), .in20(X20), .in21(X21), .in22(X22), .in23(X23), .in24(X24), .in25(X25),
    .in26(X26), .in27(X27), .in28(X28), .in29(X29), .in30(X30), .in31(X31), .out(rs1_data), .sel(rs1));
  Register #(.width(32)) u_x8 (.D(write_data), .en(WE8), .clk(CLK), .Q(X8));  // open: clr
  Register #(.width(32)) u_x9 (.D(write_data), .en(WE9), .clk(CLK), .Q(X9));  // open: clr
  Register #(.width(32)) u_x10 (.D(write_data), .en(WE10), .clk(CLK), .Q(X10));  // open: clr
  Register #(.width(32)) u_x11 (.D(write_data), .en(WE11), .clk(CLK), .Q(X11));  // open: clr
  Register #(.width(32)) u_x12 (.D(write_data), .en(WE12), .clk(CLK), .Q(X12));  // open: clr
  Register #(.width(32)) u_x13 (.D(write_data), .en(WE13), .clk(CLK), .Q(X13));  // open: clr
  Register #(.width(32)) u_x14 (.D(write_data), .en(WE14), .clk(CLK), .Q(X14));  // open: clr
  Register #(.width(32)) u_x15 (.D(write_data), .en(WE15), .clk(CLK), .Q(X15));  // open: clr
  Multiplexer #(.select(5), .width(32)) multiplexer_2 (
    .in0(X0), .in1(X1), .in2(X2), .in3(X3), .in4(X4), .in5(X5), .in6(X6), .in7(X7), .in8(X8), .in9(X9),
    .in10(X10), .in11(X11), .in12(X12), .in13(X13), .in14(X14), .in15(X15), .in16(X16), .in17(X17),
    .in18(X18), .in19(X19), .in20(X20), .in21(X21), .in22(X22), .in23(X23), .in24(X24), .in25(X25),
    .in26(X26), .in27(X27), .in28(X28), .in29(X29), .in30(X30), .in31(X31), .out(rs2_data), .sel(rs2));
  Register #(.width(32)) u_x16 (.D(write_data), .en(WE16), .clk(CLK), .Q(X16));  // open: clr
  Register #(.width(32)) u_x17 (.D(write_data), .en(WE17), .clk(CLK), .Q(X17));  // open: clr
  Register #(.width(32)) u_x18 (.D(write_data), .en(WE18), .clk(CLK), .Q(X18));  // open: clr
  Register #(.width(32)) u_x19 (.D(write_data), .en(WE19), .clk(CLK), .Q(X19));  // open: clr
  Register #(.width(32)) u_x20 (.D(write_data), .en(WE20), .clk(CLK), .Q(X20));  // open: clr
  Register #(.width(32)) u_x21 (.D(write_data), .en(WE21), .clk(CLK), .Q(X21));  // open: clr
  Register #(.width(32)) u_x22 (.D(write_data), .en(WE22), .clk(CLK), .Q(X22));  // open: clr
  Register #(.width(32)) u_x23 (.D(write_data), .en(WE23), .clk(CLK), .Q(X23));  // open: clr
  Demultiplexer #(.select(5)) demultiplexer_1 (
    .out0(demultiplexer_1_out0), .out1(WE1), .out2(WE2), .out3(WE3), .out4(WE4), .out5(WE5), .out6(WE6),
    .out7(WE7), .out8(WE8), .out9(WE9), .out10(WE10), .out11(WE11), .out12(WE12), .out13(WE13), .out14(WE14),
    .out15(WE15), .out16(WE16), .out17(WE17), .out18(WE18), .out19(WE19), .out20(WE20), .out21(WE21),
    .out22(WE22), .out23(WE23), .out24(WE24), .out25(WE25), .out26(WE26), .out27(WE27), .out28(WE28),
    .out29(WE29), .out30(WE30), .out31(WE31), .in(write), .sel(rd));
  Register #(.width(32)) u_x24 (.D(write_data), .en(WE24), .clk(CLK), .Q(X24));  // open: clr
  Register #(.width(32)) u_x25 (.D(write_data), .en(WE25), .clk(CLK), .Q(X25));  // open: clr
  Register #(.width(32)) u_x26 (.D(write_data), .en(WE26), .clk(CLK), .Q(X26));  // open: clr
  Register #(.width(32)) u_x27 (.D(write_data), .en(WE27), .clk(CLK), .Q(X27));  // open: clr
  Register #(.width(32)) u_x28 (.D(write_data), .en(WE28), .clk(CLK), .Q(X28));  // open: clr
  Register #(.width(32)) u_x29 (.D(write_data), .en(WE29), .clk(CLK), .Q(X29));  // open: clr
  Register #(.width(32)) u_x30 (.D(write_data), .en(WE30), .clk(CLK), .Q(X30));  // open: clr
  Register #(.width(32)) u_x31 (.D(write_data), .en(WE31), .clk(CLK), .Q(X31));  // open: clr

  // Other names for the same wires on the sheet: wb_data[31:0] = write_data

  // Notes on the sheet:
  //   Read port 1: x[rs1] -> rs1_data
  //   RegisterFile
  //   32 registers x 32 bits. x0 always loads the constant 0, so it always reads 0.
  //   Write: wb_data goes to every register; the DMX turns on only WE[rd] when write = 1.
  //   Read: two 32:1 multiplexers pick x[rs1] and x[rs2] (asynchronous, no clock needed).
  //   Read port 2: x[rs2] -> rs2_data
  //   Write decoder: rd -> WE of one register
endmodule

module ImmGen (
  input  [31:0] Instruction,
  input  [2:0] ImmSel,
  output [31:0] Imm
);

  wire [31:0] bit_extender_1_out, bit_extender_2_out, bit_extender_3_out, bit_extender_4_out;

  assign bit_extender_1_out = {{20{Instruction[31]}}, Instruction[31:20]};  // Bit_Extender bit_extender_1
  assign bit_extender_2_out = {{20{Instruction[31]}}, {Instruction[31:25], Instruction[11:7]}};  // Bit_Extender bit_extender_2
  assign bit_extender_3_out = {{19{Instruction[31]}}, {Instruction[31], Instruction[7], Instruction[30:25], Instruction[11:8], 1'b0}};  // Bit_Extender bit_extender_3
  assign bit_extender_4_out = {{11{Instruction[31]}}, {Instruction[31], Instruction[19:12], Instruction[20], Instruction[30:21], 1'b0}};  // Bit_Extender bit_extender_4
  Multiplexer #(.select(3), .width(32)) multiplexer_1 (
    .in0(bit_extender_1_out), .in1(bit_extender_2_out), .in2(bit_extender_3_out),
    .in3({Instruction[31:12], {12{1'b0}}}), .in4(bit_extender_4_out), .out(Imm), .sel(ImmSel));  // open: in5, in6, in7

  // Notes on the sheet:
  //   imm = instr[31:20]
  //   imm = instr[31:25], instr[11:7]
  //   imm = instr[31], [7], [30:25], [11:8], 0
  //   imm = instr[31:12] << 12
  //   low 12 bits are zero (12 zero bits appended)
  //   imm = instr[31], [19:12], [20], [30:21], 0
  //   bit 0 is always 0 (offsets are even)
  //   I-type
  //   S-type
  //   B-type
  //   U-type
  //   J-type
  //   ImmGen
  //   Rebuilds the 32-bit immediate from the instruction bits; ImmSel picks the format.
  //   ImmSel: 0 I   1 S   2 B   3 U   4 J
  //   All results are sign-extended to 32 bits.
endmodule

module MainControl (
  input  [6:0] opcode,
  output RegWrite,
  output ALUSrc,
  output MemWrite,
  output MemRead,
  output IsBranch,
  output [1:0] ALUOp,
  output [2:0] ImmSel,
  output [1:0] ASel,
  output [1:0] WBSel,
  output IsJAL,
  output IsJALR
);

  wire as_a, as_b, IsI, IsR, rw_a, rw_b;

  Comparator #(.mode("unsigned"), .width(7)) comparator_1 (.a(opcode), .b(7'b0110011), .eq(IsR));  // open: gt, lt
  Comparator #(.mode("unsigned"), .width(7)) comparator_2 (.a(opcode), .b(7'b0010011), .eq(IsI));  // open: gt, lt
  Comparator #(.mode("unsigned"), .width(7)) comparator_3 (.a(opcode), .b(7'b0000011), .eq(MemRead));  // open: gt, lt
  Comparator #(.mode("unsigned"), .width(7)) comparator_4 (.a(opcode), .b(7'b0100011), .eq(MemWrite));  // open: gt, lt
  Comparator #(.mode("unsigned"), .width(7)) comparator_5 (.a(opcode), .b(7'b1100011), .eq(IsBranch));  // open: gt, lt
  Comparator #(.mode("unsigned"), .width(7)) comparator_6 (.a(opcode), .b(7'b0110111), .eq(ASel[1]));  // open: gt, lt
  Comparator #(.mode("unsigned"), .width(7)) comparator_7 (.a(opcode), .b(7'b0010111), .eq(ASel[0]));  // open: gt, lt
  Comparator #(.mode("unsigned"), .width(7)) comparator_8 (.a(opcode), .b(7'b1101111), .eq(ImmSel[2]));  // open: gt, lt
  Comparator #(.mode("unsigned"), .width(7)) comparator_9 (.a(opcode), .b(7'b1100111), .eq(IsJALR));  // open: gt, lt
  or or_1 (rw_a, IsR, IsI, MemRead);
  or or_2 (rw_b, ASel[1], ASel[0], ImmSel[2]);
  or or_3 (as_a, IsI, MemRead, MemWrite);
  or or_4 (as_b, ASel[1], ASel[0], IsJALR);
  or or_5 (ALUOp[0], IsI, IsBranch);
  or or_6 (ALUOp[1], IsR, IsI);
  or or_7 (ImmSel[0], MemWrite, ASel[1], ASel[0]);
  or or_8 (ImmSel[1], IsBranch, ASel[1], ASel[0]);
  or or_9 (WBSel[1], ImmSel[2], IsJALR);
  or or_10 (RegWrite, rw_a, rw_b, IsJALR);
  or or_11 (ALUSrc, as_a, as_b);

  assign IsJAL = ImmSel[2];
  assign WBSel[0] = MemRead;

  // Other names for the same wires on the sheet: IsAuipc = ASel[0]; IsLui = ASel[1]; IsStore = MemWrite;
  //   IsLoad = MemRead

  // Notes on the sheet:
  //   opcode 0x33 = R-type
  //   opcode 0x13 = I-type ALU
  //   opcode 0x03 = load
  //   opcode 0x23 = store
  //   opcode 0x63 = branch
  //   opcode 0x37 = LUI
  //   opcode 0x17 = AUIPC
  //   opcode 0x6F = JAL
  //   opcode 0x67 = JALR
  //   MainControl
  //   Compares opcode with each instruction class (left) and combines the flags into control signals (right).
  //   RegWrite: every class that writes rd
  //   ALUSrc = 1: ALU operand B is the immediate
  //   ALUOp: 00 add (load/store/LUI/AUIPC/jumps)  01 sub (branch)  10 R-type  11 I-type
  //   ImmSel: 000 I   001 S (store)   010 B (branch)   011 U (LUI, AUIPC)   100 J (JAL)
  //   ASel (ALU operand A): 00 rs1   01 PC (AUIPC)   10 zero (LUI)
  //   WBSel (value written to rd): 00 ALU result   01 memory   10 PC + 4 (JAL, JALR)
endmodule

module ALUControl (
  input  [6:0] funct7,
  input  [1:0] ALUOp,
  input  [2:0] funct3,
  output [3:0] ALUCtrl
);

  wire [3:0] multiplexer_1_out, multiplexer_2_out, multiplexer_3_out, multiplexer_4_out;

  Multiplexer #(.width(4)) multiplexer_1 (.in0(4'b0110), .in1(4'b0111), .out(multiplexer_1_out), .sel(funct7[5]));
  Multiplexer #(.width(4)) multiplexer_2 (.in0(4'b0000), .in1(4'b0001), .out(multiplexer_2_out), .sel(funct7[5]));
  Multiplexer #(.select(3), .width(4)) multiplexer_3 (
    .in0(multiplexer_2_out), .in1(4'b0101), .in2(4'b1000), .in3(4'b1001), .in4(4'b0100),
    .in5(multiplexer_1_out), .in6(4'b0011), .in7(4'b0010), .out(multiplexer_3_out), .sel(funct3));
  Multiplexer #(.select(3), .width(4)) multiplexer_4 (
    .in0(4'b0000), .in1(4'b0101), .in2(4'b1000), .in3(4'b1001), .in4(4'b0100), .in5(multiplexer_1_out),
    .in6(4'b0011), .in7(4'b0010), .out(multiplexer_4_out), .sel(funct3));
  Multiplexer #(.select(2), .width(4)) multiplexer_5 (
    .in0(4'b0000), .in1(4'b0001), .in2(multiplexer_3_out), .in3(multiplexer_4_out), .out(ALUCtrl), .sel(ALUOp));

  // Notes on the sheet:
  //   ADDI 0000
  //   SLLI 0101
  //   SLTI 1000
  //   SLTIU 1001
  //   XORI 0100
  //   ANDI 0010
  //   ORI 0011
  //   SRL 0110
  //   SRA 0111
  //   ADD 0000
  //   SUB 0001
  //   SLL 0101
  //   SLT 1000
  //   SLTU 1001
  //   XOR 0100
  //   OR 0011
  //   AND 0010
  //   ALUControl
  //   ALUOp 00 = ADD (load/store)   01 = SUB (branch)   10 = R-type   11 = I-type
  //   R-type and I-type pick the operation from funct3 (funct7 separates ADD/SUB and SRL/SRA).
  //   R-dec
endmodule

module Memory (
  input  [31:0] Address,
  input  [31:0] write_data,
  input  MemWrite,
  input  CLK,
  input  [2:0] funct3,
  output [31:0] read_data
);

  wire [31:0] wnew, word;

  RAM #(.addrWidth(8), .asyncread("true"), .dataWidth(32), .enables("line")) ram_1 (
    .addr(Address[9:2]), .we(MemWrite), .clk(CLK), .din(wnew), .dout(word));
  StoreMerge storemerge_1 (
    .old_word(word), .write_data(write_data), .funct3(funct3), .boff(Address[1:0]), .new_word(wnew));
  LoadExtract loadextract_1 (.word(word), .boff(Address[1:0]), .funct3(funct3), .read_data(read_data));

  // Other names for the same wires on the sheet: boff[1:0] = Address[1:0]; widx[7:0] = Address[9:2]

  // Notes on the sheet:
  //   Address[1:0] = byte in the word, Address[9:2] = word index
  //   Memory
  //   Data RAM 256 x 32 with asynchronous read.  Loads: lb lh lw lbu lhu.  Stores: sb sh sw (read-modify-write of one word).
  //   RAM: writes on the clock edge when MemWrite = 1
  //   StoreMerge: new word to write
  //   LoadExtract: value delivered to the CPU
endmodule

module BranchUnit (
  input  [31:0] rs1_data,
  input  [31:0] rs2_data,
  input  IsBranch,
  input  [2:0] funct3,
  output branch_taken
);

  wire cond, eq, ges, geu, lts, ltu, ne;

  Comparator #(.mode("unsigned"), .width(32)) comparator_1 (.a(rs1_data), .b(rs2_data), .eq(eq), .lt(ltu));  // open: gt
  Comparator #(.width(32)) comparator_2 (.a(rs1_data), .b(rs2_data), .lt(lts));  // open: gt, eq
  not not_1 (ne, eq);
  not not_2 (geu, ltu);
  not not_3 (ges, lts);
  Multiplexer #(.select(3), .width(1)) multiplexer_1 (
    .in0(eq), .in1(ne), .in2(1'b0), .in3(1'b0), .in4(lts), .in5(ges), .in6(ltu), .in7(geu), .out(cond),
    .sel(funct3));
  and and_1 (branch_taken, IsBranch, cond);

  // Notes on the sheet:
  //   BranchUnit
  //   Decides whether a conditional branch is taken: funct3 picks the comparison, IsBranch enables it.
  //   unsigned compare
  //   signed compare
  //   funct3: 000 beq  001 bne  100 blt  101 bge  110 bltu  111 bgeu
endmodule

module LoadExtract (
  input  [31:0] word,
  input  [1:0] boff,
  input  [2:0] funct3,
  output [31:0] read_data
);

  wire [7:0] ldbyte;
  wire [15:0] ldhalf;
  wire [31:0] lb, lbu, lh, lhu;

  Multiplexer #(.select(2), .width(8)) multiplexer_1 (
    .in0(word[7:0]), .in1(word[15:8]), .in2(word[23:16]), .in3(word[31:24]), .out(ldbyte), .sel(boff));
  Multiplexer #(.select(1), .width(16)) multiplexer_2 (
    .in0(word[15:0]), .in1(word[31:16]), .out(ldhalf), .sel(boff[1]));
  assign lb = {{24{ldbyte[7]}}, ldbyte};  // Bit_Extender bit_extender_1
  assign lbu = {{24{1'b0}}, ldbyte};  // Bit_Extender bit_extender_2
  assign lh = {{16{ldhalf[15]}}, ldhalf};  // Bit_Extender bit_extender_3
  assign lhu = {{16{1'b0}}, ldhalf};  // Bit_Extender bit_extender_4
  Multiplexer #(.select(3), .width(32)) multiplexer_3 (
    .in0(lb), .in1(lh), .in2(word), .in3(word), .in4(lbu), .in5(lhu), .in6(word), .in7(word),
    .out(read_data), .sel(funct3));

  // Other names for the same wires on the sheet: by0[7:0] = word[7:0]; hw0[15:0] = word[15:0]; by1[7:0] = word[15:8];
  //   by2[7:0] = word[23:16]; hw1[15:0] = word[31:16]; by3[7:0] = word[31:24]

  // Notes on the sheet:
  //   LoadExtract
  //   Picks the loaded byte / halfword out of the 32-bit word and extends it: lb lh lw lbu lhu.
  //   byte selected by Address[1:0]
  //   halfword selected by Address[1]
  //   funct3: 000 lb  001 lh  010 lw  100 lbu  101 lhu
endmodule

module StoreMerge (
  input  [31:0] old_word,
  input  [31:0] write_data,
  input  [2:0] funct3,
  input  [1:0] boff,
  output [31:0] new_word
);

  wire [3:0] en;
  wire [7:0] src1, src2, src3;

  Multiplexer #(.select(2), .width(8)) multiplexer_1 (
    .in0(write_data[7:0]), .in1(write_data[15:8]), .in2(write_data[15:8]), .in3(write_data[15:8]),
    .out(src1), .sel(funct3[1:0]));
  Multiplexer #(.select(2), .width(8)) multiplexer_2 (
    .in0(write_data[7:0]), .in1(write_data[7:0]), .in2(write_data[23:16]), .in3(write_data[23:16]),
    .out(src2), .sel(funct3[1:0]));
  Multiplexer #(.select(2), .width(8)) multiplexer_3 (
    .in0(write_data[7:0]), .in1(write_data[15:8]), .in2(write_data[31:24]), .in3(write_data[31:24]),
    .out(src3), .sel(funct3[1:0]));
  ROM #(.addrWidth(4), .dataWidth(4)) rom_1 (.addr({funct3[1:0], boff}), .data(en));
  Multiplexer #(.select(1), .width(8)) multiplexer_4 (
    .in0(old_word[7:0]), .in1(write_data[7:0]), .out(new_word[7:0]), .sel(en[0]));
  Multiplexer #(.select(1), .width(8)) multiplexer_5 (
    .in0(old_word[15:8]), .in1(src1), .out(new_word[15:8]), .sel(en[1]));
  Multiplexer #(.select(1), .width(8)) multiplexer_6 (
    .in0(old_word[23:16]), .in1(src2), .out(new_word[23:16]), .sel(en[2]));
  Multiplexer #(.select(1), .width(8)) multiplexer_7 (
    .in0(old_word[31:24]), .in1(src3), .out(new_word[31:24]), .sel(en[3]));

  // Other names for the same wires on the sheet: enaddr[3:0] = {funct3[1:0], boff}; size[1:0] = funct3[1:0];
  //   nb0[7:0] = new_word[7:0]; nb1[7:0] = new_word[15:8]; nb2[7:0] = new_word[23:16]; nb3[7:0] = new_word[31:24];
  //   ob0[7:0] = old_word[7:0]; ob1[7:0] = old_word[15:8]; ob2[7:0] = old_word[23:16]; ob3[7:0] = old_word[31:24];
  //   wd0[7:0] = write_data[7:0]; wd1[7:0] = write_data[15:8]; wd2[7:0] = write_data[23:16];
  //   wd3[7:0] = write_data[31:24]

  // Notes on the sheet:
  //   size = funct3[1:0]: 00 byte  01 half  10 word
  //   StoreMerge
  //   A store writes a whole RAM word, so keep the old bytes that are not written: sb, sh, sw.
  //   source byte for lane 1 / 2 / 3
  //   byte enables: row = {size, Address[1:0]}
  //   contents of rom_1 (hex, n*v repeats v):
  //   1 2 4 8 3 3 c c f f f f f f f f
  //   byte 0001 0010 0100 1000 | half 0011 0011 1100 1100 | word 1111
  //   lane i = enable ? new byte : old byte
endmodule

module ForwardingUnit (
  input  [4:0] rs1_ex,
  input  [4:0] rs2_ex,
  input  [4:0] rd_mem,
  input  RegWrite_mem,
  input  [4:0] rd_wb,
  input  RegWrite_wb,
  output [1:0] ForwardA,
  output [1:0] ForwardB
);

  wire mem_eq_A, mem_eq_B, mem_is_x0, mem_ok0, mem_valid, not_mem_A, not_mem_B, wb_eq_A, wb_eq_B, wb_hit_A,
       wb_hit_B, wb_is_x0, wb_ok0, wb_valid;

  Comparator #(.mode("unsigned"), .width(5)) comparator_1 (.a(rd_mem), .b({5{1'b0}}), .eq(mem_is_x0));  // open: gt, lt
  Comparator #(.mode("unsigned"), .width(5)) comparator_2 (.a(rd_wb), .b({5{1'b0}}), .eq(wb_is_x0));  // open: gt, lt
  Comparator #(.mode("unsigned"), .width(5)) comparator_3 (.a(rd_mem), .b(rs1_ex), .eq(mem_eq_A));  // open: gt, lt
  Comparator #(.mode("unsigned"), .width(5)) comparator_4 (.a(rd_wb), .b(rs1_ex), .eq(wb_eq_A));  // open: gt, lt
  Comparator #(.mode("unsigned"), .width(5)) comparator_5 (.a(rd_mem), .b(rs2_ex), .eq(mem_eq_B));  // open: gt, lt
  Comparator #(.mode("unsigned"), .width(5)) comparator_6 (.a(rd_wb), .b(rs2_ex), .eq(wb_eq_B));  // open: gt, lt
  not not_1 (mem_ok0, mem_is_x0);
  not not_2 (wb_ok0, wb_is_x0);
  and and_1 (mem_valid, RegWrite_mem, mem_ok0);
  and and_2 (wb_valid, RegWrite_wb, wb_ok0);
  and and_3 (ForwardA[1], mem_valid, mem_eq_A);
  and and_4 (wb_hit_A, wb_valid, wb_eq_A);
  and and_5 (ForwardB[1], mem_valid, mem_eq_B);
  and and_6 (wb_hit_B, wb_valid, wb_eq_B);
  not not_3 (not_mem_A, ForwardA[1]);
  not not_4 (not_mem_B, ForwardB[1]);
  and and_7 (ForwardA[0], wb_hit_A, not_mem_A);
  and and_8 (ForwardB[0], wb_hit_B, not_mem_B);

  // Other names for the same wires on the sheet: from_wb_A = ForwardA[0]; from_mem_A = ForwardA[1];
  //   from_wb_B = ForwardB[0]; from_mem_B = ForwardB[1]

  // Notes on the sheet:
  //   ForwardingUnit
  //   Pipeline data hazards: take an operand of the EX stage from a later stage instead of the register file.
  //   operand A (rs1): EX/MEM has priority over MEM/WB
  //   operand B (rs2)
  //   a stage can forward only if it writes a register other than x0
  //   Forward: 00 register file   01 from MEM/WB   10 from EX/MEM
endmodule

module HazardUnit (
  input  MemRead_ex,
  input  [4:0] rd_ex,
  input  [4:0] rs1_id,
  input  [4:0] rs2_id,
  output stall
);

  wire hit1, hit2, rd_is_x0, rd_ok, uses;

  Comparator #(.mode("unsigned"), .width(5)) comparator_1 (.a(rd_ex), .b({5{1'b0}}), .eq(rd_is_x0));  // open: gt, lt
  Comparator #(.mode("unsigned"), .width(5)) comparator_2 (.a(rd_ex), .b(rs1_id), .eq(hit1));  // open: gt, lt
  Comparator #(.mode("unsigned"), .width(5)) comparator_3 (.a(rd_ex), .b(rs2_id), .eq(hit2));  // open: gt, lt
  not not_1 (rd_ok, rd_is_x0);
  or or_1 (uses, hit1, hit2);
  and and_1 (stall, MemRead_ex, rd_ok, uses);

  // Notes on the sheet:
  //   HazardUnit
  //   Load-use hazard: the instruction in ID needs a value that the load in EX has not read from memory yet -> stall 1 cycle.
  //   rd of the load matches a source of the next instruction
  //   stall = load in EX AND rd != x0 AND (rd == rs1 OR rd == rs2)
endmodule

module Pipeline (
  input  RESET
);

  wire ALUSrc_ex, ALUSrc_id, branch_taken, bubble, CLK, CLK_n, pc_src_ex, run, stall;
  wire [1:0] ALUOp_ex, ALUOp_id, ASel_ex, ASel_id, ForwardA, ForwardB;
  wire [2:0] ctrl_wb, funct3_ex, funct3_id, funct3_mem, ImmSel_id;
  wire [3:0] ALUCtrl;
  wire [4:0] ctrl_mem, rd_ex, rd_id, rd_mem, rd_wb, rs1_ex, rs1_id, rs2_ex, rs2_id;
  wire [6:0] funct7_ex, funct7_id, opcode_id;
  wire [12:0] ctrl_ex, ctrl_id, ctrl_in;
  wire [31:0] alu_a, alu_b, alu_result_ex, alu_result_mem, alu_result_wb, fwd_mem_val, imm_ex, imm_id,
       instr_id, instr_if, instr_in, jalr_target, mem_rdata_mem, mem_rdata_wb, next_pc, opA, opB, pc_ex,
       pc_id, pc_if, pc_plus4_ex, pc_plus4_if, pc_plus4_mem, pc_plus4_wb, pc_target, rs1_data_ex,
       rs1_data_id, rs2_data_ex, rs2_data_id, store_data_mem, target_ex, wb_data;

  Clock clock_1 (.out(CLK));
  not not_1 (CLK_n, CLK);
  Register #(.width(32)) PC (.D(next_pc), .en(run), .clk(CLK), .Q(pc_if), .clr(RESET));
  // Probe on pc_if
  Adder #(.width(32)) adder_1 (.a(pc_if), .b(32'h4), .out(pc_plus4_if));  // open: cin, cout
  ROM #(.addrWidth(8), .dataWidth(32)) rom_1 (.addr(pc_if[9:2]), .data(instr_if));
  Multiplexer #(.select(1), .width(32)) multiplexer_1 (
    .in0(pc_plus4_if), .in1(target_ex), .out(next_pc), .sel(pc_src_ex));
  Multiplexer #(.select(1), .width(32)) multiplexer_2 (
    .in0(instr_if), .in1({32{1'b0}}), .out(instr_in), .sel(pc_src_ex));
  not not_2 (run, stall);
  Register #(.width(32)) u_pc_id (.D(pc_if), .en(run), .clk(CLK), .Q(pc_id));  // open: clr
  Register #(.width(32)) u_instr_id (.D(instr_in), .en(run), .clk(CLK), .Q(instr_id));  // open: clr
  // Probe on instr_id
  // Probe on stall
  or or_1 (bubble, stall, pc_src_ex);
  Multiplexer #(.select(1), .width(13)) multiplexer_3 (
    .in0({ctrl_id[12:9], ASel_id, ALUOp_id, ctrl_id[4:2], ALUSrc_id, ctrl_id[0]}), .in1({13{1'b0}}),
    .out(ctrl_in), .sel(bubble));
  InstructionDecode instructiondecode_1 (
    .Instruction(instr_id), .funct7(funct7_id), .rs2(rs2_id), .rs1(rs1_id), .funct3(funct3_id), .rd(rd_id),
    .opcode(opcode_id));
  MainControl maincontrol_1 (
    .opcode(opcode_id), .RegWrite(ctrl_id[0]), .ALUSrc(ALUSrc_id), .MemWrite(ctrl_id[2]),
    .MemRead(ctrl_id[3]), .IsBranch(ctrl_id[4]), .ALUOp(ALUOp_id), .ImmSel(ImmSel_id), .ASel(ASel_id),
    .WBSel(ctrl_id[10:9]), .IsJAL(ctrl_id[11]), .IsJALR(ctrl_id[12]));
  ImmGen immgen_1 (.Instruction(instr_id), .ImmSel(ImmSel_id), .Imm(imm_id));
  RegisterFile registerfile_1 (
    .write_data(wb_data), .CLK(CLK_n), .write(ctrl_wb[0]), .rd(rd_wb), .rs1(rs1_id), .rs2(rs2_id),
    .rs1_data(rs1_data_id), .rs2_data(rs2_data_id));
  HazardUnit hazardunit_1 (.MemRead_ex(ctrl_ex[3]), .rd_ex(rd_ex), .rs1_id(rs1_id), .rs2_id(rs2_id), .stall(stall));
  // Probe on pc_src_ex
  Register #(.width(32)) u_pc_ex (.D(pc_id), .en(1'b1), .clk(CLK), .Q(pc_ex));  // open: clr
  Register #(.width(32)) u_rs1_data_ex (.D(rs1_data_id), .en(1'b1), .clk(CLK), .Q(rs1_data_ex));  // open: clr
  Register #(.width(32)) u_rs2_data_ex (.D(rs2_data_id), .en(1'b1), .clk(CLK), .Q(rs2_data_ex));  // open: clr
  Register #(.width(32)) u_imm_ex (.D(imm_id), .en(1'b1), .clk(CLK), .Q(imm_ex));  // open: clr
  Register #(.width(5)) u_rs1_ex (.D(rs1_id), .en(1'b1), .clk(CLK), .Q(rs1_ex));  // open: clr
  Register #(.width(5)) u_rs2_ex (.D(rs2_id), .en(1'b1), .clk(CLK), .Q(rs2_ex));  // open: clr
  Register #(.width(5)) u_rd_ex (.D(rd_id), .en(1'b1), .clk(CLK), .Q(rd_ex));  // open: clr
  Register #(.width(3)) u_funct3_ex (.D(funct3_id), .en(1'b1), .clk(CLK), .Q(funct3_ex));  // open: clr
  Register #(.width(7)) u_funct7_ex (.D(funct7_id), .en(1'b1), .clk(CLK), .Q(funct7_ex));  // open: clr
  Register #(.width(13)) u_ctrl_ex (
    .D(ctrl_in), .en(1'b1), .clk(CLK),
    .Q({ctrl_ex[12:9], ASel_ex, ALUOp_ex, ctrl_ex[4:2], ALUSrc_ex, ctrl_ex[0]}));  // open: clr
  // Probe on ForwardA
  Multiplexer #(.select(1), .width(32)) multiplexer_4 (
    .in0(alu_result_mem), .in1(pc_plus4_mem), .out(fwd_mem_val), .sel(ctrl_mem[4]));
  Multiplexer #(.select(2), .width(32)) multiplexer_5 (
    .in0(rs1_data_ex), .in1(wb_data), .in2(fwd_mem_val), .in3(rs1_data_ex), .out(opA), .sel(ForwardA));
  Multiplexer #(.select(2), .width(32)) multiplexer_6 (
    .in0(rs2_data_ex), .in1(wb_data), .in2(fwd_mem_val), .in3(rs2_data_ex), .out(opB), .sel(ForwardB));
  Multiplexer #(.select(2), .width(32)) multiplexer_7 (
    .in0(opA), .in1(pc_ex), .in2({32{1'b0}}), .in3({32{1'b0}}), .out(alu_a), .sel(ASel_ex));
  Multiplexer #(.select(1), .width(32)) multiplexer_8 (.in0(opB), .in1(imm_ex), .out(alu_b), .sel(ALUSrc_ex));
  // Probe on ForwardB
  ForwardingUnit forwardingunit_1 (
    .rs1_ex(rs1_ex), .rs2_ex(rs2_ex), .rd_mem(rd_mem), .RegWrite_mem(ctrl_mem[0]), .rd_wb(rd_wb),
    .RegWrite_wb(ctrl_wb[0]), .ForwardA(ForwardA), .ForwardB(ForwardB));
  ALUControl alucontrol_1 (.funct7(funct7_ex), .ALUOp(ALUOp_ex), .funct3(funct3_ex), .ALUCtrl(ALUCtrl));
  ALU alu_1 (.rs1_data(alu_a), .rs2_data(alu_b), .ALU_Ctrl(ALUCtrl), .result(alu_result_ex));
  BranchUnit branchunit_1 (
    .rs1_data(opA), .rs2_data(opB), .IsBranch(ctrl_ex[4]), .funct3(funct3_ex), .branch_taken(branch_taken));
  // Probe on alu_result_ex
  Adder #(.width(32)) adder_2 (.a(pc_ex), .b(imm_ex), .out(pc_target));  // open: cin, cout
  assign jalr_target = alu_result_ex & 32'hfffffffe;  // AND_Gate and_1, 32 bits wide
  Multiplexer #(.select(1), .width(32)) multiplexer_9 (
    .in0(pc_target), .in1(jalr_target), .out(target_ex), .sel(ctrl_ex[12]));
  or or_2 (pc_src_ex, branch_taken, ctrl_ex[11], ctrl_ex[12]);
  Adder #(.width(32)) adder_3 (.a(pc_ex), .b(32'h4), .out(pc_plus4_ex));  // open: cin, cout
  Register #(.width(32)) u_alu_result_mem (.D(alu_result_ex), .en(1'b1), .clk(CLK), .Q(alu_result_mem));  // open: clr
  Register #(.width(32)) u_store_data_mem (.D(opB), .en(1'b1), .clk(CLK), .Q(store_data_mem));  // open: clr
  Register #(.width(32)) u_pc_plus4_mem (.D(pc_plus4_ex), .en(1'b1), .clk(CLK), .Q(pc_plus4_mem));  // open: clr
  Register #(.width(5)) u_rd_mem (.D(rd_ex), .en(1'b1), .clk(CLK), .Q(rd_mem));  // open: clr
  Register #(.width(3)) u_funct3_mem (.D(funct3_ex), .en(1'b1), .clk(CLK), .Q(funct3_mem));  // open: clr
  Register #(.width(5)) u_ctrl_mem (
    .D({ctrl_ex[10:9], ctrl_ex[3:2], ctrl_ex[0]}), .en(1'b1), .clk(CLK), .Q(ctrl_mem));  // open: clr
  // Probe on wb_data
  Memory memory_1 (
    .Address(alu_result_mem), .write_data(store_data_mem), .MemWrite(ctrl_mem[1]), .CLK(CLK),
    .funct3(funct3_mem), .read_data(mem_rdata_mem));
  Register #(.width(32)) u_alu_result_wb (.D(alu_result_mem), .en(1'b1), .clk(CLK), .Q(alu_result_wb));  // open: clr
  Register #(.width(32)) u_mem_rdata_wb (.D(mem_rdata_mem), .en(1'b1), .clk(CLK), .Q(mem_rdata_wb));  // open: clr
  Register #(.width(32)) u_pc_plus4_wb (.D(pc_plus4_mem), .en(1'b1), .clk(CLK), .Q(pc_plus4_wb));  // open: clr
  Register #(.width(5)) u_rd_wb (.D(rd_mem), .en(1'b1), .clk(CLK), .Q(rd_wb));  // open: clr
  Register #(.width(3)) u_ctrl_wb (.D({ctrl_mem[4:3], ctrl_mem[0]}), .en(1'b1), .clk(CLK), .Q(ctrl_wb));  // open: clr
  Multiplexer #(.select(2), .width(32)) multiplexer_10 (
    .in0(alu_result_wb), .in1(mem_rdata_wb), .in2(pc_plus4_wb), .in3({32{1'b0}}), .out(wb_data),
    .sel(ctrl_wb[2:1]));

  // Other names for the same wires on the sheet: ctrl_ex (some bits) = {ASel_ex, ALUOp_ex, ALUSrc_ex};
  //   IsBranch_ex = ctrl_ex[4]; IsJAL_ex = ctrl_ex[11]; IsJALR_ex = ctrl_ex[12]; RegWrite_id = ctrl_id[0];
  //   ctrl_id (some bits) = {ASel_id, ALUOp_id, ALUSrc_id}; MemWrite_id = ctrl_id[2]; MemRead_id = ctrl_id[3];
  //   IsBranch_id = ctrl_id[4]; WBSel_id[1:0] = ctrl_id[10:9]; IsJAL_id = ctrl_id[11]; IsJALR_id = ctrl_id[12];
  //   MemWrite_mem = ctrl_mem[1]; MemRead_mem = ctrl_mem[2];
  //   ctrl_mem_in[4:0] = {ctrl_ex[10:9], ctrl_ex[3:2], ctrl_ex[0]}; RegWrite_ex = ctrl_ex[0];
  //   MemWrite_ex = ctrl_ex[2]; MemRead_ex = ctrl_ex[3]; WBSel_ex[1:0] = ctrl_ex[10:9]; RegWrite_wb = ctrl_wb[0];
  //   WBSel_wb[1:0] = ctrl_wb[2:1]; ctrl_wb_in[2:0] = {ctrl_mem[4:3], ctrl_mem[0]}; RegWrite_mem = ctrl_mem[0];
  //   WBSel_mem[1:0] = ctrl_mem[4:3]; WBSel1_mem = ctrl_mem[4]; pc_word[7:0] = pc_if[9:2]

  // Notes on the sheet:
  //   Clock: Ctrl+F9 = 1 full cycle
  //   RESET = 1 holds PC at 0
  //   CLK_n: the register file writes on the falling edge,
  //   so WB can write and ID can read in the same cycle
  //   PC register (holds while stalled)
  //   IF - Instruction Fetch
  //   BẢNG THEO DÕI (probe): xem các giá trị này sau mỗi lần bấm Ctrl+F9
  //   next PC: PC+4, or the branch / jump target from EX
  //   a taken branch / jump turns the fetched instruction into a bubble (0)
  //   run = not stall: PC and IF/ID only advance when run = 1
  //   PC: địa chỉ đang fetch (đứng yên = stall)
  //   (nhảy khi pc_src_ex = 1)
  //   PC + 4
  //   contents of rom_1 (hex, n*v repeats v):
  //   00000513 00a00593 00b50533 fff58593 fe059ce3 00a02023 00002603 010000ef 40a606b3 0646a713 0000006f
  //   00c60633 00008067 00000000 00000000 00000000
  //   Instruction ROM 256 x 32
  //   IF/ID registers
  //   instr_id: lệnh đang ở tầng ID
  //   (0 = bubble bị flush)
  //   control word (13 bits)
  //   bubble = stall OR flush: the control word becomes 0 (a NOP)
  //   InstructionDecode
  //   MainControl
  //   ImmGen
  //   RegisterFile (writes on CLK_n)
  //   HazardUnit: load-use stall
  //   stall = 1: load-use, PC và IF/ID
  //   đứng yên 1 chu kỳ
  //   ID - Decode / Register Read
  //   pc_src_ex = 1: rẽ nhánh/JAL/JALR,
  //   flush 2 lệnh đã fetch
  //   ID/EX registers
  //   RV32I 5-stage pipeline - top level
  //   IF > ID > EX > MEM > WB with pipeline registers between the stages.  Forwarding (EX), load-use stall (ID) and branch / jump flush (EX).
  //   Tunnels with the same name are the same wire.  Suffix _id _ex _mem _wb = the stage a value belongs to.
  //   control word of the instruction in EX
  //   value in EX/MEM that can be forwarded (ALU result, or PC+4 of JAL/JALR)
  //   operand A: 00 register  01 MEM/WB  10 EX/MEM
  //   operand B / store data: same choices
  //   ForwardA: 00 reg, 01 MEM/WB,
  //   10 EX/MEM (toán hạng A)
  //   EX - Execute
  //   ALU A: rs1 / PC (auipc) / 0 (lui)
  //   ALU B: rs2 / imm
  //   ForwardingUnit
  //   ForwardB: 00 reg, 01 MEM/WB,
  //   10 EX/MEM (toán hạng B)
  //   ALUControl
  //   ALU
  //   BranchUnit
  //   branch / JAL target = PC + imm
  //   JALR target = (rs1 + imm), bit 0 cleared
  //   pc_src_ex = redirect the PC (taken branch, JAL, JALR) and flush IF/ID + ID/EX
  //   link address PC+4
  //   alu_result_ex: kết quả ALU
  //   của lệnh đang ở tầng EX
  //   pack RegWrite, MemWrite, MemRead, WBSel
  //   EX/MEM registers
  //   wb_data: giá trị ghi vào thanh ghi
  //   ở tầng WB
  //   control word of the instruction in MEM
  //   WBSel bit 1: result is PC+4
  //   MEM - Data Memory
  //   Memory
  //   pack RegWrite, WBSel
  //   MEM/WB registers
  //   control word of the instruction in WB
  //   WB - Write Back
  //   WBSel: 00 ALU  01 memory  10 PC+4
  //   wb_data goes to the register file (ID) and is also forwarded to EX
endmodule
